# Fritzing sketch differential (saved by Fritzing 1.0.4)
circuit board: 3.99892cm x 3.6661cm
breadboards: 1

parts:
  TL082 = IC, DIP package, 8 pins [chip_label=TL082]
  R1 = Resistor [tolerance=±5% power=0.25W resistance=10k package=THT]
  R2 = Resistor [tolerance=±5% power=0.25W resistance=10k package=THT]
  R3 = Resistor [tolerance=±5% power=0.25W resistance=10k package=THT]
  R4 = Resistor [tolerance=±5% power=0.25W resistance=10k package=THT]
  Rg1 = Resistor [tolerance=±5% power=0.25W resistance=10k package=THT]
  Rf1 = Resistor [tolerance=±5% power=0.25W resistance=10k package=THT]
  Rf2 = Resistor [tolerance=±5% power=0.25W resistance=10k package=THT]
  Rg2 = Resistor [tolerance=±5% power=0.25W resistance=10k package=THT]

nets:
  N1: TL082.pin1, Rf1.Pin_0
  N2: TL082.pin2, R2.Pin_0, Rf1.Pin_1
  N3: TL082.pin3, R1.Pin_0, Rg1.Pin_0
  N4: TL082.pin5, R3.Pin_0, Rg2.Pin_0
  N5: TL082.pin6, R4.Pin_0, Rf2.Pin_1
  N6: TL082.pin7, Rf2.Pin_0

notes:
  𝗩𝗰𝗰+
  𝗩𝗰𝗰-
  𝗴𝗻𝗱
  𝗩𝟭
  𝗩𝟮
  𝗩𝟯
  𝗩𝟰
  𝗼𝘂𝘁𝟭
  𝗼𝘂𝘁𝟮
  𝗗𝗜𝗙𝗙
  𝗥𝟭
  𝗥𝟮
  𝗥𝟯
  𝗧𝗟𝟬𝟴𝟮
  𝗥𝟳
  𝗥𝟲
  𝗥𝟱
  𝗥𝟴
  𝗥𝟰
