# Fritzing sketch integrator (saved by Fritzing 1.0.4)
circuit board: 4.07324cm x 2.79529cm
breadboards: 1

parts:
  TL082 = IC, DIP package, 8 pins [chip_label=IC]
  R1 = Resistor [tolerance=±5% power=0.25W resistance=220 package=THT]
  C1 = Ceramic Capacitor [capacitance=100nF voltage=35V package="200 mil [THT, multilayer]"]
  R2 = Resistor [tolerance=±5% power=0.25W resistance=220 package=THT]
  R3 = Resistor [tolerance=±5% power=0.25W resistance=220 package=THT]
  R4 = Resistor [tolerance=±5% power=0.25W resistance=220 package=THT]
  C2 = Ceramic Capacitor [capacitance=100nF voltage=35V package="200 mil [THT, multilayer]"]

nets:
  N1: TL082.pin1, C1.1, R2.Pin_1
  N2: TL082.pin2, R1.Pin_0, C1.0, R2.Pin_0
  N3: TL082.pin3, TL082.pin5
  N4: TL082.pin6, R3.Pin_1, R4.Pin_1, C2.1
  N5: TL082.pin7, R4.Pin_0, C2.0

notes:
  gnd
  Vcc-
  Vcc+
  out2
  out1
  in1
  in2
  INT
