# Fritzing sketch sum (saved by Fritzing 1.0.4)
circuit board: 4.20139cm x 3.12997cm
breadboards: 1

parts:
  part = IC, DIP package, 8 pins
  Rg1 = Resistor [tolerance=±5% power=0.25W resistance=220 package=THT]
  𝗥𝟯 = Resistor [tolerance=±5% power=0.25W resistance=220 package=THT]
  R1 = Resistor [tolerance=±5% power=0.25W resistance=220 package=THT]
  R2 = Resistor [tolerance=±5% power=0.25W resistance=220 package=THT]
  R3 = Resistor [tolerance=±5% power=0.25W resistance=220 package=THT]
  R4 = Resistor [tolerance=±5% power=0.25W resistance=220 package=THT]
  Rf2 = Resistor [tolerance=±5% power=0.25W resistance=220 package=THT]
  Rg2 = Resistor [tolerance=±5% power=0.25W resistance=220 package=THT]

nets:
  N1: part.pin1, 𝗥𝟯.Pin_0
  N2: part.pin2, Rg1.Pin_1, 𝗥𝟯.Pin_1
  N3: part.pin3, R1.Pin_0, R2.Pin_0
  N4: part.pin5, R3.Pin_0, R4.Pin_0
  N5: part.pin6, Rf2.Pin_1, Rg2.Pin_1
  N6: part.pin7, Rf2.Pin_0

notes:
  𝗩𝟮
  𝗩𝗰𝗰+
  𝗩𝗰𝗰-
  𝗴𝗻𝗱
  𝗩𝟭
  𝗼𝘂𝘁𝟭
  𝗼𝘂𝘁𝟮
  𝗩𝟯
  𝗩𝟰
  𝗦𝗨𝗠
  𝗥𝟭
  𝗥𝟮
  𝗥𝟰
  𝗥𝟯
  𝗥𝟱
  𝗥𝟲
  𝗥𝟴
  𝗥𝟳
  𝗧𝗟𝟬𝟴𝟮
